// Logisim project Reloj.circ as structural Verilog: 3 circuits, main circuit main
module main (
  input  in_1,
  input  in_2,
  input  in_3,
  input  in_4,
  input  in_5,
  input  in_6,
  input  in_7,
  input  in_8,
  input  in_9,
  input  in_10,
  input  in_11
);

  wire and_1_out, and_2_out, and_3_out, and_4_out, and_5_out, and_6_out, and_7_out, and_8_out, and_9_out,
       and_10_out, and_11_out, and_12_out, and_13_out, and_14_out, and_15_out, and_16_out, and_17_out,
       and_18_out, and_19_out, and_20_out, and_21_out, and_22_out, and_23_out, and_24_out, and_25_out,
       and_26_out, and_27_out, and_28_out, and_29_out, and_30_out, and_31_out, and_32_out, and_33_out,
       and_34_out, and_35_out, and_36_out, and_37_out, and_38_out, and_39_out, and_40_out, and_41_out,
       and_42_out, and_43_out, and_44_out, and_45_out, bdc_1_fa, bdc_1_fb, bdc_1_fc, bdc_1_fd, bdc_1_fe,
       bdc_1_ff, bdc_1_fg, bdc_2_fa, bdc_2_fb, bdc_2_fc, bdc_2_fd, bdc_2_fe, bdc_2_ff, bdc_2_fg, bdc_3_fa,
       bdc_3_fb, bdc_3_fc, bdc_3_fd, bdc_3_fe, bdc_3_ff, bdc_3_fg, bdc_4_fa, bdc_4_fb, bdc_4_fc, bdc_4_fd,
       bdc_4_fe, bdc_4_ff, bdc_4_fg, bdc_5_fa, bdc_5_fb, bdc_5_fc, bdc_5_fd, bdc_5_fe, bdc_5_ff, bdc_5_fg,
       bdc_6_fa, bdc_6_fb, bdc_6_fc, bdc_6_fd, bdc_6_fe, bdc_6_ff, bdc_6_fg, clock_1_out, ffd_enable_1_q,
       ffd_enable_2_q, ffd_enable_3_q, ffd_enable_4_q, ffd_enable_5_q, ffd_enable_6_q, ffd_enable_7_q,
       ffd_enable_8_q, ffd_enable_9_q, ffd_enable_10_q, ffd_enable_11_q, ffd_enable_12_q, ffd_enable_13_q,
       ffd_enable_14_q, ffd_enable_15_q, ffd_enable_16_q, ffd_enable_17_q, ffd_enable_18_q, ffd_enable_19_q,
       not_1_out, not_2_out, not_3_out, not_4_out, not_5_out, not_6_out, not_7_out, not_8_out, not_9_out,
       not_10_out, not_11_out, not_12_out, not_13_out, not_14_out, not_15_out, or_1_out, or_2_out, or_3_out,
       or_4_out, or_5_out, or_6_out, or_7_out, or_8_out, or_9_out, or_10_out, or_11_out, or_12_out,
       or_13_out, or_14_out, or_15_out, or_16_out, or_17_out, or_18_out, or_19_out, or_20_out, or_21_out,
       or_22_out, or_23_out, or_24_out, or_25_out, or_26_out, or_27_out;

  LED led_1 (.in(ffd_enable_1_q));
  FFD_enable ffd_enable_1 (.D(not_5_out), .Enable(or_7_out), .Clock(or_6_out), .Q(ffd_enable_1_q));
  not not_1 (not_1_out, ffd_enable_3_q);
  not not_2 (not_2_out, ffd_enable_2_q);
  not not_3 (not_3_out, ffd_enable_4_q);
  not not_4 (not_4_out, ffd_enable_5_q);
  not not_5 (not_5_out, ffd_enable_1_q);
  and and_1 (and_1_out, ffd_enable_2_q, not_3_out, not_4_out);
  and and_2 (and_2_out, ffd_enable_4_q, ffd_enable_5_q, ffd_enable_3_q);
  and and_3 (and_3_out, not_2_out, ffd_enable_3_q, not_3_out);
  and and_4 (and_4_out, not_1_out, ffd_enable_4_q, ffd_enable_5_q);
  and and_5 (and_5_out, ffd_enable_4_q, not_4_out, ffd_enable_3_q);
  and and_6 (and_6_out, not_2_out, not_3_out, ffd_enable_5_q);
  and and_7 (and_7_out, ffd_enable_4_q, not_4_out, not_2_out);
  and and_8 (and_8_out, not_2_out, not_4_out);
  and and_9 (and_9_out, ffd_enable_2_q, not_1_out, not_4_out);
  or or_1 (or_1_out, and_1_out, and_2_out);
  or or_2 (or_2_out, and_3_out, and_4_out, and_5_out);
  or or_3 (or_3_out, and_6_out, and_7_out);
  or or_4 (or_4_out, and_8_out, and_9_out);
  BDC bdc_1 (
    .d0(ffd_enable_1_q), .Fa(bdc_1_fa), .Fb(bdc_1_fb), .Fc(bdc_1_fc), .Fd(bdc_1_fd), .Fe(bdc_1_fe),
    .Ff(bdc_1_ff), .Fg(bdc_1_fg));  // open: d3, d2, d1
  _7_Segment_Display u_7_segment_display_1 (
    .g(bdc_1_fg), .f(bdc_1_ff), .a(bdc_1_fa), .b(bdc_1_fb), .e(bdc_1_fe), .d(bdc_1_fd), .c(bdc_1_fc));  // open: dp
  FFD_enable ffd_enable_2 (.D(or_1_out), .Enable(or_5_out), .Clock(or_8_out), .Q(ffd_enable_2_q));
  FFD_enable ffd_enable_3 (.D(or_2_out), .Enable(or_5_out), .Clock(or_8_out), .Q(ffd_enable_3_q));
  FFD_enable ffd_enable_4 (.D(or_3_out), .Enable(or_5_out), .Clock(or_8_out), .Q(ffd_enable_4_q));
  FFD_enable ffd_enable_5 (.D(or_4_out), .Enable(or_5_out), .Clock(or_8_out), .Q(ffd_enable_5_q));
  or or_5 (or_5_out, and_11_out, in_11);
  or or_6 (or_6_out, in_5, or_8_out);
  or or_7 (or_7_out, in_6, and_10_out);
  LED led_2 (.in(ffd_enable_2_q));
  LED led_3 (.in(ffd_enable_3_q));
  LED led_4 (.in(ffd_enable_4_q));
  LED led_5 (.in(ffd_enable_5_q));
  or or_8 (or_8_out, clock_1_out, in_10);
  and and_10 (and_10_out, ffd_enable_5_q, ffd_enable_2_q);
  and and_11 (and_11_out, and_14_out, and_15_out);
  and and_12 (and_12_out, ffd_enable_4_q, ~ffd_enable_5_q, ~ffd_enable_3_q);  // AND_Gate
  BDC bdc_2 (
    .d3(ffd_enable_2_q), .d2(ffd_enable_3_q), .d1(ffd_enable_4_q), .d0(ffd_enable_5_q), .Fa(bdc_2_fa),
    .Fb(bdc_2_fb), .Fc(bdc_2_fc), .Fd(bdc_2_fd), .Fe(bdc_2_fe), .Ff(bdc_2_ff), .Fg(bdc_2_fg));
  and and_13 (and_13_out, and_12_out, ffd_enable_1_q);
  LED led_6 (.in(ffd_enable_6_q));
  LED led_7 (.in(ffd_enable_7_q));
  LED led_8 (.in(ffd_enable_8_q));
  and and_14 (and_14_out, ffd_enable_8_q, ffd_enable_6_q);
  and and_15 (and_15_out, ffd_enable_9_q, ffd_enable_12_q);
  _7_Segment_Display u_7_segment_display_2 (
    .g(bdc_2_fg), .f(bdc_2_ff), .a(bdc_2_fa), .b(bdc_2_fb), .e(bdc_2_fe), .d(bdc_2_fd), .c(bdc_2_fc));  // open: dp
  FFD_enable ffd_enable_6 (.D(or_9_out), .Enable(or_18_out), .Clock(or_17_out), .Q(ffd_enable_6_q));
  FFD_enable ffd_enable_7 (.D(or_10_out), .Enable(or_18_out), .Clock(or_17_out), .Q(ffd_enable_7_q));
  FFD_enable ffd_enable_8 (.D(not_10_out), .Enable(or_18_out), .Clock(or_17_out), .Q(ffd_enable_8_q));
  not not_6 (not_6_out, ffd_enable_10_q);
  not not_7 (not_7_out, ffd_enable_9_q);
  not not_8 (not_8_out, ffd_enable_11_q);
  not not_9 (not_9_out, ffd_enable_12_q);
  or or_9 (or_9_out, and_25_out, and_26_out);
  or or_10 (or_10_out, and_27_out, and_28_out);
  not not_10 (not_10_out, ffd_enable_8_q);
  and and_16 (and_16_out, ffd_enable_9_q, not_8_out, not_9_out);
  and and_17 (and_17_out, ffd_enable_11_q, ffd_enable_12_q, ffd_enable_10_q);
  and and_18 (and_18_out, not_7_out, ffd_enable_10_q, not_8_out);
  and and_19 (and_19_out, not_6_out, ffd_enable_11_q, ffd_enable_12_q);
  and and_20 (and_20_out, ffd_enable_11_q, not_9_out, ffd_enable_10_q);
  and and_21 (and_21_out, not_7_out, not_8_out, ffd_enable_12_q);
  and and_22 (and_22_out, ffd_enable_11_q, not_9_out, not_7_out);
  and and_23 (and_23_out, not_7_out, not_9_out);
  and and_24 (and_24_out, ffd_enable_9_q, not_6_out, not_9_out);
  or or_11 (or_11_out, and_16_out, and_17_out);
  or or_12 (or_12_out, and_18_out, and_19_out, and_20_out);
  or or_13 (or_13_out, and_21_out, and_22_out);
  or or_14 (or_14_out, and_23_out, and_24_out);
  and and_25 (and_25_out, ffd_enable_6_q, ~ffd_enable_8_q, ~ffd_enable_7_q);  // AND_Gate
  and and_26 (and_26_out, ~ffd_enable_6_q, ffd_enable_7_q, ffd_enable_8_q);  // AND_Gate
  and and_27 (and_27_out, ~ffd_enable_8_q, ffd_enable_7_q);  // AND_Gate
  and and_28 (and_28_out, ~ffd_enable_7_q, ~ffd_enable_6_q, ffd_enable_8_q);  // AND_Gate
  BDC bdc_3 (
    .d2(ffd_enable_6_q), .d1(ffd_enable_7_q), .d0(ffd_enable_8_q), .Fa(bdc_3_fa), .Fb(bdc_3_fb),
    .Fc(bdc_3_fc), .Fd(bdc_3_fd), .Fe(bdc_3_fe), .Ff(bdc_3_ff), .Fg(bdc_3_fg));  // open: d3
  _7_Segment_Display u_7_segment_display_3 (
    .g(bdc_3_fg), .f(bdc_3_ff), .a(bdc_3_fa), .b(bdc_3_fb), .e(bdc_3_fe), .d(bdc_3_fd), .c(bdc_3_fc));  // open: dp
  FFD_enable ffd_enable_9 (.D(or_11_out), .Enable(or_16_out), .Clock(or_15_out), .Q(ffd_enable_9_q));
  FFD_enable ffd_enable_10 (.D(or_12_out), .Enable(or_16_out), .Clock(or_15_out), .Q(ffd_enable_10_q));
  FFD_enable ffd_enable_11 (.D(or_13_out), .Enable(or_16_out), .Clock(or_15_out), .Q(ffd_enable_11_q));
  FFD_enable ffd_enable_12 (.D(or_14_out), .Enable(or_16_out), .Clock(or_15_out), .Q(ffd_enable_12_q));
  or or_15 (or_15_out, clock_1_out, in_8);
  or or_16 (or_16_out, and_30_out, in_9);
  or or_17 (or_17_out, in_2, or_15_out);
  or or_18 (or_18_out, in_4, and_29_out);
  LED led_9 (.in(ffd_enable_9_q));
  LED led_10 (.in(ffd_enable_10_q));
  LED led_11 (.in(ffd_enable_11_q));
  LED led_12 (.in(ffd_enable_12_q));
  and and_29 (and_29_out, ffd_enable_12_q, ffd_enable_9_q);
  and and_30 (and_30_out, and_31_out, and_45_out);
  BDC bdc_4 (
    .d3(ffd_enable_9_q), .d2(ffd_enable_10_q), .d1(ffd_enable_11_q), .d0(ffd_enable_12_q), .Fa(bdc_4_fa),
    .Fb(bdc_4_fb), .Fc(bdc_4_fc), .Fd(bdc_4_fd), .Fe(bdc_4_fe), .Ff(bdc_4_ff), .Fg(bdc_4_fg));
  _7_Segment_Display u_7_segment_display_4 (
    .g(bdc_4_fg), .f(bdc_4_ff), .a(bdc_4_fa), .b(bdc_4_fb), .e(bdc_4_fe), .d(bdc_4_fd), .c(bdc_4_fc));  // open: dp
  and and_31 (and_31_out, ffd_enable_15_q, ffd_enable_13_q);
  LED led_13 (.in(ffd_enable_13_q));
  LED led_14 (.in(ffd_enable_14_q));
  LED led_15 (.in(ffd_enable_15_q));
  FFD_enable ffd_enable_13 (.D(or_20_out), .Enable(or_27_out), .Clock(or_26_out), .Q(ffd_enable_13_q));
  FFD_enable ffd_enable_14 (.D(or_21_out), .Enable(or_27_out), .Clock(or_26_out), .Q(ffd_enable_14_q));
  FFD_enable ffd_enable_15 (.D(not_15_out), .Enable(or_27_out), .Clock(or_26_out), .Q(ffd_enable_15_q));
  not not_11 (not_11_out, ffd_enable_17_q);
  not not_12 (not_12_out, ffd_enable_16_q);
  or or_19 (or_19_out, in_7, and_13_out);
  not not_13 (not_13_out, ffd_enable_19_q);
  not not_14 (not_14_out, ffd_enable_18_q);
  or or_20 (or_20_out, and_41_out, and_42_out);
  or or_21 (or_21_out, and_43_out, and_44_out);
  and and_32 (and_32_out, ffd_enable_16_q, not_14_out, not_13_out);
  and and_33 (and_33_out, ffd_enable_18_q, ffd_enable_19_q, ffd_enable_17_q);
  and and_34 (and_34_out, not_12_out, ffd_enable_17_q, not_14_out);
  and and_35 (and_35_out, not_11_out, ffd_enable_18_q, ffd_enable_19_q);
  and and_36 (and_36_out, ffd_enable_18_q, not_13_out, ffd_enable_17_q);
  and and_37 (and_37_out, not_12_out, not_14_out, ffd_enable_19_q);
  and and_38 (and_38_out, ffd_enable_18_q, not_13_out, not_12_out);
  and and_39 (and_39_out, not_12_out, not_13_out);
  and and_40 (and_40_out, ffd_enable_16_q, not_11_out, not_13_out);
  not not_15 (not_15_out, ffd_enable_15_q);
  and and_41 (and_41_out, ffd_enable_13_q, ~ffd_enable_15_q, ~ffd_enable_14_q);  // AND_Gate
  and and_42 (and_42_out, ~ffd_enable_13_q, ffd_enable_14_q, ffd_enable_15_q);  // AND_Gate
  and and_43 (and_43_out, ~ffd_enable_15_q, ffd_enable_14_q);  // AND_Gate
  and and_44 (and_44_out, ~ffd_enable_14_q, ~ffd_enable_13_q, ffd_enable_15_q);  // AND_Gate
  or or_22 (or_22_out, and_32_out, and_33_out);
  or or_23 (or_23_out, and_34_out, and_35_out, and_36_out);
  Clock clock_1 (.out(clock_1_out));
  or or_24 (or_24_out, and_37_out, and_38_out);
  or or_25 (or_25_out, and_39_out, and_40_out);
  BDC bdc_5 (
    .d2(ffd_enable_13_q), .d1(ffd_enable_14_q), .d0(ffd_enable_15_q), .Fa(bdc_5_fa), .Fb(bdc_5_fb),
    .Fc(bdc_5_fc), .Fd(bdc_5_fd), .Fe(bdc_5_fe), .Ff(bdc_5_ff), .Fg(bdc_5_fg));  // open: d3
  _7_Segment_Display u_7_segment_display_5 (
    .g(bdc_5_fg), .f(bdc_5_ff), .a(bdc_5_fa), .b(bdc_5_fb), .e(bdc_5_fe), .d(bdc_5_fd), .c(bdc_5_fc));  // open: dp
  FFD_enable ffd_enable_16 (.D(or_22_out), .Enable(or_19_out), .Clock(clock_1_out), .Q(ffd_enable_16_q));
  FFD_enable ffd_enable_17 (.D(or_23_out), .Enable(or_19_out), .Clock(clock_1_out), .Q(ffd_enable_17_q));
  FFD_enable ffd_enable_18 (.D(or_24_out), .Enable(or_19_out), .Clock(clock_1_out), .Q(ffd_enable_18_q));
  FFD_enable ffd_enable_19 (.D(or_25_out), .Enable(or_19_out), .Clock(clock_1_out), .Q(ffd_enable_19_q));
  or or_26 (or_26_out, in_1, clock_1_out);
  or or_27 (or_27_out, in_3, and_45_out);
  LED led_16 (.in(ffd_enable_16_q));
  LED led_17 (.in(ffd_enable_17_q));
  LED led_18 (.in(ffd_enable_18_q));
  LED led_19 (.in(ffd_enable_19_q));
  and and_45 (and_45_out, ffd_enable_19_q, ffd_enable_16_q);
  BDC bdc_6 (
    .d3(ffd_enable_16_q), .d2(ffd_enable_17_q), .d1(ffd_enable_18_q), .d0(ffd_enable_19_q), .Fa(bdc_6_fa),
    .Fb(bdc_6_fb), .Fc(bdc_6_fc), .Fd(bdc_6_fd), .Fe(bdc_6_fe), .Ff(bdc_6_ff), .Fg(bdc_6_fg));
  _7_Segment_Display u_7_segment_display_6 (
    .g(bdc_6_fg), .f(bdc_6_ff), .a(bdc_6_fa), .b(bdc_6_fb), .e(bdc_6_fe), .d(bdc_6_fd), .c(bdc_6_fc));  // open: dp

  // Notes on the sheet:
  //   d0
  //   -d3
  //   -d2
  //   -d1
  //   -d0
  //   d1
  //   d3
  //   d0
  //   d2
  //   d3
  //   d2
  //   d1
  //   d0
  //   Horas
  //   d2
  //   d1
  //   d0
  //   -d3
  //   -d2
  //   -d1
  //   -d0
  //   d1
  //   d3
  //   d0
  //   d2
  //   Minutos
  //   d3
  //   d2
  //   d1
  //   d0
  //   d2
  //   d1
  //   d0
  //   -d2
  //   -d3
  //   -d0
  //   -d1
  //   d0
  //   d1
  //   d3
  //   d2
  //   Segundos
  //   d3
  //   d2
  //   d1
  //   d0
endmodule

module BDC (
  input  d3,
  input  d2,
  input  d1,
  input  d0,
  output Fa,
  output Fb,
  output Fc,
  output Fd,
  output Fe,
  output Ff,
  output Fg
);

  wire and_1_out, and_2_out, and_3_out, and_4_out, and_5_out, and_6_out, and_7_out, and_8_out, and_9_out,
       and_10_out, and_11_out, and_12_out, and_13_out, and_14_out, and_15_out, and_16_out, and_17_out,
       and_18_out, and_19_out, and_20_out, and_21_out, and_22_out, and_23_out, and_24_out, and_25_out,
       and_26_out;

  and and_1 (and_1_out, ~d0, ~d2, ~d3);  // AND_Gate
  and and_2 (and_2_out, ~d3, d1);  // AND_Gate
  and and_3 (and_3_out, ~d1, d0, d2);  // AND_Gate
  and and_4 (and_4_out, ~d1, d3);  // AND_Gate
  and and_5 (and_5_out, d0, d1);
  and and_6 (and_6_out, ~d0, ~d1);  // AND_Gate
  and and_7 (and_7_out, ~d1, d3);  // AND_Gate
  and and_8 (and_8_out, ~d2, ~d3);  // AND_Gate
  and and_9 (and_9_out, d0, d1);
  and and_10 (and_10_out, d1, d2);
  and and_11 (and_11_out, ~d0, ~d2, ~d3);  // AND_Gate
  and and_12 (and_12_out, ~d2, ~d3, d1);  // AND_Gate
  and and_13 (and_13_out, ~d1, d0, d2);  // AND_Gate
  and and_14 (and_14_out, ~d0, d1);  // AND_Gate
  and and_15 (and_15_out, ~d0, d3);  // AND_Gate
  and and_16 (and_16_out, ~d3, ~d2, ~d0);  // AND_Gate
  and and_17 (and_17_out, ~d0, ~d1, d3);  // AND_Gate
  and and_18 (and_18_out, ~d0, d1, d2);  // AND_Gate
  and and_19 (and_19_out, ~d0, ~d1);  // AND_Gate
  and and_20 (and_20_out, ~d1, d3);  // AND_Gate
  and and_21 (and_21_out, ~d1, d2);  // AND_Gate
  and and_22 (and_22_out, ~d0, d1, d2);  // AND_Gate
  and and_23 (and_23_out, ~d3, ~d2, d1);  // AND_Gate
  and and_24 (and_24_out, ~d0, d1, d2);  // AND_Gate
  and and_25 (and_25_out, ~d1, d2);  // AND_Gate
  and and_26 (and_26_out, ~d1, d3);  // AND_Gate
  or or_1 (Fc, and_9_out, ~d1, and_10_out);  // OR_Gate
  or or_2 (Fd, and_11_out, and_12_out, and_13_out, and_14_out, and_15_out);
  or or_3 (Fg, and_23_out, and_24_out, and_25_out, and_26_out);
  or or_4 (Fa, and_1_out, and_2_out, and_3_out, and_4_out);
  or or_5 (Fb, and_5_out, and_6_out, and_7_out, and_8_out);
  or or_6 (Fe, and_16_out, and_17_out, and_18_out);
  or or_7 (Ff, and_19_out, and_20_out, and_21_out, and_22_out);
endmodule

module FFD_enable (
  input  D,
  input  Enable,
  input  Clock,
  output Q
);

  wire and_1_out, and_2_out, not_1_out, or_1_out;

  not not_1 (not_1_out, Enable);
  and and_1 (and_1_out, Q, not_1_out);
  and and_2 (and_2_out, D, Enable);
  D_Flip_Flop d_ff_1 (.D(or_1_out), .clk(Clock), .Q(Q));  // open: Qn, preset, reset
  or or_1 (or_1_out, and_1_out, and_2_out);
endmodule
